# Fritzing sketch sketch (saved by Fritzing 0.9.3b)
breadboards: 1

parts:
  Part1 = Arduino Uno (Rev3)
  R1 = Resistor [tolerance=±5% resistance=220 package=THT]
  R2 = Resistor [tolerance=±5% resistance=220 package=THT]
  R3 = Resistor [tolerance=±5% resistance=220 package=THT]
  LED1 = LED - 5mm [color="Red (633nm)" package="5 mm [THT]"]
  LED2 = LED - 5mm [color="Yellow (595nm)" package="5 mm [THT]"]
  LED3 = LED - 5mm [color="Green (560nm)" package="5 mm [THT]"]
  Generic_4x4_button_keypad1 = Generic 4x4 Keypad
  IR_VS1838B = TSOP312.., 314.. [package=THT]

nets:
  N1: Part1.A0, IR_VS1838B.Data
  N2: Part1.D8, Generic_4x4_button_keypad1.R3
  N3: Part1.D9_PWM, Generic_4x4_button_keypad1.R4
  N4: Part1.D10_PWM/SS, LED1.anode
  N5: Part1.D11_PWM/MOSI, LED2.anode
  N6: Part1.D12/MISO, LED3.anode
  GND: Part1.GND, R1.Pin_1, R2.Pin_1, R3.Pin_1, IR_VS1838B.GND
  N7: Part1.D2, Generic_4x4_button_keypad1.C1
  N8: Part1.D3_PWM, Generic_4x4_button_keypad1.C2
  N9: Part1.D4, Generic_4x4_button_keypad1.C3
  N10: Part1.D5_PWM, Generic_4x4_button_keypad1.C4
  N11: Part1.D6_PWM, Generic_4x4_button_keypad1.R1
  N12: Part1.D7, Generic_4x4_button_keypad1.R2
  N13: Part1.5V, IR_VS1838B.Vs
  N14: R1.Pin_0, LED3.cathode
  N15: R2.Pin_0, LED2.cathode
  N16: R3.Pin_0, LED1.cathode

custom parts:
  Generic 4x4 Keypad: generic 4x4 keypad 4 rows of four 6 mm tact switches cheap and nasty but works
